// Logisim project cpu.circ as structural Verilog: 2 circuits, main circuit main
module main (
);

  wire A_IN, A_OUT, AB_SEL0, AB_SEL1, AB_SEL2, adder_2_cout, ADDR_ABUS_OUT, ADDR_INH, ADDR_INL, ALU_ADD,
       ALU_AND, ALU_C, ALU_NONE, ALU_OR, ALU_OUT, ALU_RSH, ALU_SEL0, ALU_SEL1, ALU_SEL2, ALU_SUB, ALU_XOR,
       and_1_out, and_3_out, and_4_out, and_5_out, and_6_out, and_7_out, and_8_out, and_9_out, and_10_out,
       and_11_out, and_12_out, and_13_out, and_16_out, and_17_out, and_18_out, and_19_out, B_IN, B_OUT, C,
       C_IN, C_JMP, C_OUT, CIE, CLK, counter_5_p2, counter_5_p3, d_ff_1_q, D_IN, D_OUT, DB_SEL0, DB_SEL1,
       DB_SEL2, DB_SEL3, DB_TAR_SEL0, DB_TAR_SEL1, DB_TAR_SEL2, DB_TAR_SEL3, DB_TAR_SEL4, DD_IN,
       decoder_1_out0, decoder_1_out1, decoder_1_out2, decoder_1_out4, decoder_1_out5, decoder_1_out6,
       decoder_1_out7, decoder_2_out0, decoder_2_out1, decoder_2_out2, decoder_2_out3, decoder_2_out4,
       decoder_2_out5, decoder_2_out6, decoder_2_out7, decoder_3_out0, decoder_3_out1, decoder_3_out2,
       decoder_3_out3, decoder_5_out5, decoder_5_out6, decoder_6_out11, decoder_6_out12, decoder_6_out16,
       decoder_6_out18, decoder_6_out19, decoder_6_out21, decoder_7_out15, DISP_IN, DS_IN, DUMMY_DD_OUT,
       E_IN, E_OUT, F_IN, F_OUT, FLAG_INV, FLAGS_IN, FLAGS_OUT, G_IN, G_OUT, H_IN, H_OUT, HALT, INSB_HI,
       INSB_HO, INSB_O, IO_OUT, IR2_IN, IR_IN, IRQ, IRQ_ABUS_OUT, IRQ_ABUS_OUT2, JMP, MEM_OUT, MISC_SEL0,
       MISC_SEL1, MISC_SEL2, N, N_JMP, nand_1_out, not_10_out, not_11_out, not_12_out, not_13_out,
       not_14_out, not_15_out, O, O_JMP, OP_IN, or_1_out, or_2_out, or_3_out, or_4_out, or_5_out, or_6_out,
       or_7_out, or_8_out, or_12_out, OSC_out, PC_ABUS_OUT, PC_IN, PC_OUTH, PC_OUTL, RAM_IN, register_3_q,
       RESET, rgb_video_1_p3, RUN, RUN_STOP_out, SIE, SP_ABUS_OUT, SP_DEC, SP_INC, SPO_ABUS_OUT, STEP_out,
       T_RESET, T_RESET_PF, xnor_1_out, xor_1_out, xor_2_out, xor_3_out, xor_4_out, xor_5_out, xor_8_out,
       xor_9_out, Z, Z_JMP;
  wire [0:0] _4x28C16_data_2, _4x28C16_data_3, _4x28C16_data_4;
  wire [1:0] MODE2, pull_resistor_1_node;
  wire [2:0] and_20_out, rgb_video_1_p6, T_STATE;
  wire [3:0] multiplexer_1_out, multiplexer_3_out, undriven, undriven_3, undriven_5, undriven_7;
  wire [5:0] rgb_video_1_p5, U_out;
  wire [6:0] rgb_video_1_p4;
  wire [7:0] _4x28C16_data, adder_2_out, and_15_out, controlled_buffer_25_out, counter_5_p1, IR_REG, IR_REG2,
       OP_REG, or_11_out, register_2_q, register_7_q, register_8_q, register_9_q, register_10_q,
       register_11_q, register_12_q, register_13_q, register_14_q, register_15_q, rom_1_data, W_BUS, W_BUS2,
       xor_6_out, xor_7_out;
  wire [7:4] undriven_2, undriven_4, undriven_6, undriven_8;
  wire [7:7] and_14_out;
  wire [14:0] SP;
  wire [15:0] AD_BUS, adder_1_out, AR, controlled_buffer_4_out, counter_1_q;
  wire [15:15] not_8_out, not_9_out;
  wire [31:0] counter_2_q, counter_3_q;

  LED Df (.in(AR[15]));
  LED De (.in(AR[14]));
  LED Dd (.in(AR[13]));
  assign AD_BUS = ADDR_ABUS_OUT ? AR : 16'bz;  // Controlled_Buffer controlled_buffer_1
  LED Df_2 (.in(AD_BUS[15]));
  Adder #(.width(16)) adder_1 (.a({1'b0, SP}), .b({{8{1'b0}}, AR[7:0]}), .out(adder_1_out));  // open: cin, cout
  assign AD_BUS = IRQ_ABUS_OUT ? 16'hfff8 : 16'bz;  // Controlled_Buffer controlled_buffer_2
  Button L (.out(U_out[1]));
  LED Dc (.in(AR[12]));
  LED Db (.in(AR[11]));
  LED Da (.in(AR[10]));
  LED D9 (.in(AR[9]));
  LED De_2 (.in(AD_BUS[14]));
  LED Dd_2 (.in(AD_BUS[13]));
  LED Dc_2 (.in(AD_BUS[12]));
  LED Db_2 (.in(AD_BUS[11]));
  assign AD_BUS = SPO_ABUS_OUT ? adder_1_out : 16'bz;  // Controlled_Buffer controlled_buffer_3
  Decoder #(.enable("false"), .select(3)) decoder_1 (
    .out0(decoder_1_out0), .out1(decoder_1_out1), .out2(decoder_1_out2), .out4(decoder_1_out4),
    .out5(decoder_1_out5), .out6(decoder_1_out6), .out7(decoder_1_out7), .sel({ALU_SEL2, ALU_SEL1, ALU_SEL0}));  // open: out3
  Button U (.out(U_out[0]));
  Button R (.out(U_out[2]));
  Button D (.out(U_out[5]));
  LED D8 (.in(AR[8]));
  LED D7 (.in(AR[7]));
  LED D6 (.in(AR[6]));
  LED Da_2 (.in(AD_BUS[10]));
  LED D9_2 (.in(AD_BUS[9]));
  LED D8_2 (.in(AD_BUS[8]));
  LED D7_2 (.in(AD_BUS[7]));
  Button A (.out(U_out[4]));
  LED D5 (.in(AR[5]));
  LED D4 (.in(AR[4]));
  LED D3 (.in(AR[3]));
  LED D2 (.in(AR[2]));
  assign controlled_buffer_4_out = ADDR_INL ? {AR[15:8], W_BUS} : 16'bz;  // Controlled_Buffer controlled_buffer_4
  assign controlled_buffer_4_out = ADDR_INH ? {W_BUS, AR[7:0]} : 16'bz;  // Controlled_Buffer controlled_buffer_5
  or or_1 (or_1_out, ADDR_INH, ADDR_INL);
  LED D6_2 (.in(AD_BUS[6]));
  LED D5_2 (.in(AD_BUS[5]));
  LED D4_2 (.in(AD_BUS[4]));
  LED D3_2 (.in(AD_BUS[3]));
  LED D7_3 (.in(W_BUS[7]));
  LED D6_3 (.in(W_BUS[6]));
  assign W_BUS = DUMMY_DD_OUT ? {8{1'b0}} : 8'bz;  // Controlled_Buffer controlled_buffer_6
  not not_1 (ALU_RSH, decoder_1_out0);
  not not_2 (ALU_ADD, decoder_1_out1);
  not not_3 (ALU_SUB, decoder_1_out2);
  not not_4 (ALU_XOR, decoder_1_out4);
  not not_5 (ALU_AND, decoder_1_out5);
  not not_6 (ALU_OR, decoder_1_out6);
  not not_7 (ALU_NONE, decoder_1_out7);
  Button B (.out(U_out[3]));
  LED D1 (.in(AR[1]));
  LED D0 (.in(AR[0]));
  Register #(.width(16)) register_1 (.D(controlled_buffer_4_out), .en(or_1_out), .Q(AR), .clk(CLK));  // open: clr
  LED D2_2 (.in(AD_BUS[2]));
  LED D1_2 (.in(AD_BUS[1]));
  LED D0_2 (.in(AD_BUS[0]));
  LED D5_3 (.in(W_BUS[5]));
  LED D4_3 (.in(W_BUS[4]));
  LED D3_3 (.in(W_BUS[3]));
  LED D2_3 (.in(W_BUS[2]));
  assign W_BUS2 = IRQ ? {8{1'b1}} : 8'bz;  // Controlled_Buffer controlled_buffer_7
  Register register_2 (.D({2'b00, U_out}), .en(or_2_out), .Q(register_2_q), .clk(CLK));  // open: clr
  Register #(.width(1)) register_3 (.D(or_2_out), .Q(register_3_q), .clk(CLK));  // open: en, clr
  or or_2 (or_2_out, U_out[0], U_out[5], U_out[4], U_out[3], U_out[2], U_out[1]);
  LED D1_3 (.in(W_BUS[1]));
  LED D0_3 (.in(W_BUS[0]));
  assign W_BUS = IO_OUT ? register_2_q : 8'bz;  // Controlled_Buffer controlled_buffer_8
  D_Flip_Flop d_ff_1 (.D(1'b1), .Q(d_ff_1_q), .preset(SIE), .reset(or_3_out));  // open: clk, Qn
  or or_3 (or_3_out, CIE, RESET);
  not not_8 (not_8_out[15], AD_BUS[15]);
  and and_1 (and_1_out, PC_ABUS_OUT, ~IRQ);  // AND_Gate
  Button u_RESET (.out(RESET));
  Button RUN_STOP (.out(RUN_STOP_out));
  ROM #(.addrWidth(15)) rom_1 (.addr(AD_BUS[14:0]), .data(rom_1_data));
  and and_2 (IRQ, IR_IN, register_3_q, d_ff_1_q);
  LED D7_4 (.in(not_9_out[15]));
  LED D6_4 (.in(counter_1_q[14]));
  assign AD_BUS = PC_ABUS_OUT ? {not_9_out[15], counter_1_q[14:0]} : 16'bz;  // Controlled_Buffer controlled_buffer_9
  Counter #(.max('hffff), .width(16)) counter_1 (
    .load(JMP), .D({not_8_out[15], AD_BUS[14:0]}), .count(and_1_out), .Q(counter_1_q), .clk(CLK), .clr(RESET));  // open: carry
  T_Flip_Flop #(.enable("true")) t_ff_1 (
    .clk(RUN_STOP_out), .T(1'b1), .Q(RUN), .reset(RESET), .en(1'b1));  // open: Qn, preset
  xor xor_1 (xor_1_out, C, FLAG_INV);
  xor xor_2 (xor_2_out, Z, FLAG_INV);
  xor xor_3 (xor_3_out, O, FLAG_INV);
  xor xor_4 (xor_4_out, N, FLAG_INV);
  and and_3 (and_3_out, MEM_OUT, ~AD_BUS[15]);  // AND_Gate
  RAM #(.addrWidth(15), .databus("bidir")) ram_1 (.addr(AD_BUS[14:0]), .data(W_BUS));  // open: we, oe, clk
  LED D5_4 (.in(counter_1_q[13]));
  LED D4_4 (.in(counter_1_q[12]));
  LED D3_4 (.in(counter_1_q[11]));
  LED D2_4 (.in(counter_1_q[10]));
  not not_9 (not_9_out[15], counter_1_q[15]);
  Button STEP (.out(STEP_out));
  Clock OSC (.out(OSC_out));
  LED D1_4 (.in(counter_1_q[9]));
  LED D0_4 (.in(counter_1_q[8]));
  LED D7_5 (.in(counter_1_q[7]));
  Counter #(.max('hffffffff), .width(32)) counter_2 (
    .count(CLK), .Q(counter_2_q), .clk(CLK), .clr(RESET));  // open: load, D, carry
  and and_4 (and_4_out, STEP_out, ~RUN);  // AND_Gate
  and and_5 (and_5_out, RUN, OSC_out);
  or or_4 (or_4_out, HALT, 1'b0);
  or or_5 (or_5_out, PC_IN, and_6_out);
  and and_6 (and_6_out, C_JMP, xor_1_out);
  and and_7 (and_7_out, Z_JMP, xor_2_out);
  and and_8 (and_8_out, O_JMP, xor_3_out);
  or or_6 (or_6_out, and_8_out, and_9_out);
  and and_9 (and_9_out, N_JMP, xor_4_out);
  LED D6_5 (.in(counter_1_q[6]));
  LED D5_5 (.in(counter_1_q[5]));
  LED D4_5 (.in(counter_1_q[4]));
  LED D3_5 (.in(counter_1_q[3]));
  assign W_BUS = PC_OUTH ? counter_1_q[7:0] : 8'bz;  // Controlled_Buffer controlled_buffer_10
  assign W_BUS = PC_OUTL ? {not_9_out[15], counter_1_q[14:8]} : 8'bz;  // Controlled_Buffer controlled_buffer_11
  Counter #(.max('hffffffff), .width(32)) counter_3 (.Q(counter_3_q));  // open: load, D, count, carry, clk, clr
  and and_10 (and_10_out, and_5_out, ~or_4_out);  // AND_Gate
  or or_7 (or_7_out, and_7_out, or_6_out);
  assign W_BUS = FLAGS_OUT ? {4'b0000, N, O, Z, C} : 8'bz;  // Controlled_Buffer controlled_buffer_12
  and and_11 (and_11_out, MEM_OUT, AD_BUS[15]);
  and and_12 (and_12_out, ~IRQ, and_11_out);  // AND_Gate
  or or_8 (or_8_out, and_11_out, and_12_out);
  assign W_BUS = or_8_out ? rom_1_data : 8'bz;  // Controlled_Buffer controlled_buffer_13
  and and_13 (and_13_out, ~IRQ, IR_IN);  // AND_Gate
  assign W_BUS2 = and_13_out ? rom_1_data : 8'bz;  // Controlled_Buffer controlled_buffer_14
  LED D0_5 (.in(counter_1_q[0]));
  LED D2_5 (.in(counter_1_q[2]));
  LED D1_5 (.in(counter_1_q[1]));
  Comparator #(.width(32)) comparator_1 (.a(counter_2_q), .b(counter_3_q));  // open: gt, eq, lt
  or or_9 (CLK, and_4_out, and_10_out);
  or or_10 (JMP, or_5_out, or_7_out);
  Pull_Resistor pull_resistor_1 (.node(pull_resistor_1_node));
  assign W_BUS = A_OUT ? register_7_q : 8'bz;  // Controlled_Buffer controlled_buffer_15
  assign W_BUS = B_OUT ? register_8_q : 8'bz;  // Controlled_Buffer controlled_buffer_16
  assign W_BUS = C_OUT ? register_9_q : 8'bz;  // Controlled_Buffer controlled_buffer_17
  assign W_BUS = D_OUT ? register_10_q : 8'bz;  // Controlled_Buffer controlled_buffer_18
  assign W_BUS = E_OUT ? register_11_q : 8'bz;  // Controlled_Buffer controlled_buffer_19
  assign W_BUS = F_OUT ? register_12_q : 8'bz;  // Controlled_Buffer controlled_buffer_20
  assign W_BUS = G_OUT ? register_13_q : 8'bz;  // Controlled_Buffer controlled_buffer_21
  assign W_BUS = H_OUT ? register_14_q : 8'bz;  // Controlled_Buffer controlled_buffer_22
  Counter #(.max('h7), .width(3)) counter_4 (
    .load(T_RESET), .D({pull_resistor_1_node, T_RESET_PF}), .count(CLK), .Q(T_STATE), .clk(CLK), .clr(RESET));  // open: carry
  Register register_4 (.D(W_BUS2), .en(IR_IN), .Q(IR_REG), .clk(CLK));  // open: clr
  Register register_5 (.D(W_BUS), .en(IR2_IN), .Q(IR_REG2), .clk(CLK));  // open: clr
  Register register_6 (.D(W_BUS), .en(OP_IN), .Q(OP_REG), .clk(CLK));  // open: clr
  Register register_7 (.D(W_BUS), .en(A_IN), .Q(register_7_q), .clk(CLK));  // open: clr
  Register register_8 (.D(W_BUS), .en(B_IN), .Q(register_8_q), .clk(CLK));  // open: clr
  Register register_9 (.D(W_BUS), .en(C_IN), .Q(register_9_q), .clk(CLK));  // open: clr
  Register register_10 (.D(W_BUS), .en(D_IN), .Q(register_10_q), .clk(CLK));  // open: clr
  Register register_11 (.D(W_BUS), .en(E_IN), .Q(register_11_q), .clk(CLK));  // open: clr
  Register register_12 (.D(W_BUS), .en(F_IN), .Q(register_12_q), .clk(CLK));  // open: clr
  Register register_13 (.D(W_BUS), .en(G_IN), .Q(register_13_q), .clk(CLK));  // open: clr
  Register register_14 (.D(W_BUS), .en(H_IN), .Q(register_14_q), .clk(CLK));  // open: clr
  LED T0 (.in(decoder_2_out0));
  LED T1 (.in(decoder_2_out1));
  LED T2 (.in(decoder_2_out2));
  LED T3 (.in(decoder_2_out3));
  Decoder #(.select(3)) decoder_2 (
    .out0(decoder_2_out0), .out1(decoder_2_out1), .out2(decoder_2_out2), .out3(decoder_2_out3),
    .out4(decoder_2_out4), .out5(decoder_2_out5), .out6(decoder_2_out6), .out7(decoder_2_out7), .sel(T_STATE));  // open: en
  LED D7_6 (.in(IR_REG[7]));
  LED D6_6 (.in(IR_REG[6]));
  LED D5_6 (.in(IR_REG[5]));
  LED D4_6 (.in(IR_REG[4]));
  LED D7_7 (.in(IR_REG2[7]));
  LED D6_7 (.in(IR_REG2[6]));
  LED D5_7 (.in(IR_REG2[5]));
  LED D4_7 (.in(IR_REG2[4]));
  LED D7_8 (.in(OP_REG[7]));
  LED D6_8 (.in(OP_REG[6]));
  LED D5_8 (.in(OP_REG[5]));
  LED D4_8 (.in(OP_REG[4]));
  LED D7_9 (.in(register_7_q[7]));
  LED D6_9 (.in(register_7_q[6]));
  LED D5_9 (.in(register_7_q[5]));
  LED D4_9 (.in(register_7_q[4]));
  LED D7_10 (.in(register_8_q[7]));
  LED D6_10 (.in(register_8_q[6]));
  LED D5_10 (.in(register_8_q[5]));
  LED D4_10 (.in(register_8_q[4]));
  LED D7_11 (.in(register_9_q[7]));
  LED D6_11 (.in(register_9_q[6]));
  LED D5_11 (.in(register_9_q[5]));
  LED D4_11 (.in(register_9_q[4]));
  LED D7_12 (.in(register_10_q[7]));
  LED D6_12 (.in(register_10_q[6]));
  LED D5_12 (.in(register_10_q[5]));
  LED D4_12 (.in(register_10_q[4]));
  LED D7_13 (.in(register_11_q[7]));
  LED D6_13 (.in(register_11_q[6]));
  LED D5_13 (.in(register_11_q[5]));
  LED D4_13 (.in(register_11_q[4]));
  LED D7_14 (.in(register_12_q[7]));
  LED D6_14 (.in(register_12_q[6]));
  LED D5_14 (.in(register_12_q[5]));
  LED D4_14 (.in(register_12_q[4]));
  LED D7_15 (.in(register_13_q[7]));
  LED D6_15 (.in(register_13_q[6]));
  LED D5_15 (.in(register_13_q[5]));
  LED D4_15 (.in(register_13_q[4]));
  LED D7_16 (.in(register_14_q[7]));
  LED D6_16 (.in(register_14_q[6]));
  LED D5_16 (.in(register_14_q[5]));
  LED D4_16 (.in(register_14_q[4]));
  LED T4 (.in(decoder_2_out4));
  LED T5 (.in(decoder_2_out5));
  LED T6 (.in(decoder_2_out6));
  LED T7 (.in(decoder_2_out7));
  LED D3_6 (.in(IR_REG[3]));
  LED D2_6 (.in(IR_REG[2]));
  LED D1_6 (.in(IR_REG[1]));
  LED D0_6 (.in(IR_REG[0]));
  LED D3_7 (.in(IR_REG2[3]));
  LED D2_7 (.in(IR_REG2[2]));
  LED D1_7 (.in(IR_REG2[1]));
  LED D0_7 (.in(IR_REG2[0]));
  LED D3_8 (.in(OP_REG[3]));
  LED D2_8 (.in(OP_REG[2]));
  LED D1_8 (.in(OP_REG[1]));
  LED D0_8 (.in(OP_REG[0]));
  LED D3_9 (.in(register_7_q[3]));
  LED D2_9 (.in(register_7_q[2]));
  LED D1_9 (.in(register_7_q[1]));
  LED D0_9 (.in(register_7_q[0]));
  LED D3_10 (.in(register_8_q[3]));
  LED D2_10 (.in(register_8_q[2]));
  LED D1_10 (.in(register_8_q[1]));
  LED D0_10 (.in(register_8_q[0]));
  LED D3_11 (.in(register_9_q[3]));
  LED D2_11 (.in(register_9_q[2]));
  LED D1_11 (.in(register_9_q[1]));
  LED D0_11 (.in(register_9_q[0]));
  LED D3_12 (.in(register_10_q[3]));
  LED D2_12 (.in(register_10_q[2]));
  LED D1_12 (.in(register_10_q[1]));
  LED D0_12 (.in(register_10_q[0]));
  LED D3_13 (.in(register_11_q[3]));
  LED D2_13 (.in(register_11_q[2]));
  LED D1_13 (.in(register_11_q[1]));
  LED D0_13 (.in(register_11_q[0]));
  LED D3_14 (.in(register_12_q[3]));
  LED D2_14 (.in(register_12_q[2]));
  LED D1_14 (.in(register_12_q[1]));
  LED D0_14 (.in(register_12_q[0]));
  LED D3_15 (.in(register_13_q[3]));
  LED D2_15 (.in(register_13_q[2]));
  LED D1_15 (.in(register_13_q[1]));
  LED D0_15 (.in(register_13_q[0]));
  LED D3_16 (.in(register_14_q[3]));
  LED D2_16 (.in(register_14_q[2]));
  LED D1_16 (.in(register_14_q[1]));
  LED D0_16 (.in(register_14_q[0]));
  nand nand_1 (nand_1_out, ALU_SEL0, ALU_SEL1);
  and and_14 (and_14_out[7], C, ALU_C);
  // Counter #(.max('h3), .width(2)) counter_5: pin names not known; wires that end beside it: counter_5_p1, counter_5_p2, counter_5_p3, MODE2
  LED UNSINGED (.in(decoder_3_out0));
  LED SIGNED (.in(decoder_3_out1));
  Decoder #(.select(2)) decoder_3 (
    .out0(decoder_3_out0), .out1(decoder_3_out1), .out2(decoder_3_out2), .out3(decoder_3_out3), .sel(MODE2));  // open: en
  LED HEX (.in(decoder_3_out2));
  LED OCTAL (.in(decoder_3_out3));
  LED F (.in(1'b0));
  LED E (.in(SP[14]));
  assign AD_BUS = SP_ABUS_OUT ? {1'b0, SP} : 16'bz;  // Controlled_Buffer controlled_buffer_23
  assign W_BUS = ALU_OUT ? register_15_q : 8'bz;  // Controlled_Buffer controlled_buffer_24
  Register register_15 (.D(controlled_buffer_25_out), .en(nand_1_out), .Q(register_15_q), .clk(CLK));  // open: clr
  Register register_16 (.D(W_BUS), .en(DISP_IN), .Q(counter_5_p1), .clk(CLK), .clr(RESET));
  Button MODE (.out(counter_5_p3));
  LED D_2 (.in(SP[13]));
  LED u_C (.in(SP[12]));
  LED B_2 (.in(SP[11]));
  LED A_2 (.in(SP[10]));
  LED D7_17 (.in(register_15_q[7]));
  LED D6_17 (.in(register_15_q[6]));
  LED D5_17 (.in(register_15_q[5]));
  LED D4_17 (.in(register_15_q[4]));
  Register #(.width(1)) register_17 (.D(multiplexer_1_out[2]), .en(not_10_out), .Q(C), .clk(CLK), .clr(RESET));
  not not_10 (not_10_out, ALU_SEL2);
  xor xor_5 (xor_5_out, and_14_out[7], ALU_ADD);
  assign xor_6_out = OP_REG ^ {8{ALU_ADD}};  // XOR_Gate xor_6, 8 bits wide
  assign xor_7_out = OP_REG ^ W_BUS;  // XOR_Gate xor_7, 8 bits wide
  assign controlled_buffer_25_out = not_13_out ? xor_7_out : 8'bz;  // Controlled_Buffer controlled_buffer_25
  assign and_15_out = OP_REG & W_BUS;  // AND_Gate and_15, 8 bits wide
  assign controlled_buffer_25_out = not_14_out ? and_15_out : 8'bz;  // Controlled_Buffer controlled_buffer_26
  assign or_11_out = OP_REG | W_BUS;  // OR_Gate or_11, 8 bits wide
  assign controlled_buffer_25_out = not_15_out ? or_11_out : 8'bz;  // Controlled_Buffer controlled_buffer_27
  // ROM #(.addrWidth(10), .dataWidth(32)) rom_2: pin names not known; wires that end beside it: counter_5_p1, counter_5_p2, DISP_IN, {MODE2, counter_5_p1}
  _7_Segment_Display u_7_segment_display_1 (
    .g(undriven_8[7]), .f(undriven_8[6]), .a(undriven_8[5]), .b(undriven_8[4]), .e(undriven_7[3]),
    .d(undriven_7[2]), .c(undriven_7[1]), .dp(undriven_7[0]));
  _7_Segment_Display u_7_segment_display_2 (
    .g(undriven_6[7]), .f(undriven_6[6]), .a(undriven_6[5]), .b(undriven_6[4]), .e(undriven_5[3]),
    .d(undriven_5[2]), .c(undriven_5[1]), .dp(undriven_5[0]));
  LED _9 (.in(SP[9]));
  LED _8 (.in(SP[8]));
  LED _7 (.in(SP[7]));
  LED _6 (.in(SP[6]));
  or or_12 (or_12_out, SP_INC, SP_DEC);
  LED D3_17 (.in(register_15_q[3]));
  LED D2_17 (.in(register_15_q[2]));
  LED D1_17 (.in(register_15_q[1]));
  LED D0_17 (.in(register_15_q[0]));
  Register #(.width(1)) register_18 (.D(multiplexer_1_out[1]), .en(nand_1_out), .Q(Z), .clk(CLK), .clr(RESET));
  not not_11 (not_11_out, and_18_out);
  assign controlled_buffer_25_out = not_11_out ? adder_2_out : 8'bz;  // Controlled_Buffer controlled_buffer_28
  Adder adder_2 (.a(W_BUS), .b(xor_6_out), .out(adder_2_out), .cin(xor_5_out), .cout(adder_2_cout));
  xor xor_8 (xor_8_out, adder_2_cout, ALU_ADD);
  and and_16 (and_16_out, ALU_NONE, ALU_RSH);
  not not_12 (not_12_out, and_16_out);
  assign controlled_buffer_25_out = not_12_out ? {and_14_out[7], W_BUS[7:1]} : 8'bz;  // Controlled_Buffer controlled_buffer_29
  not not_13 (not_13_out, ALU_XOR);
  not not_14 (not_14_out, ALU_AND);
  not not_15 (not_15_out, ALU_OR);
  _7_Segment_Display u_7_segment_display_3 (
    .g(undriven_4[7]), .f(undriven_4[6]), .a(undriven_4[5]), .b(undriven_4[4]), .e(undriven_3[3]),
    .d(undriven_3[2]), .c(undriven_3[1]), .dp(undriven_3[0]));
  LED _5 (.in(SP[5]));
  LED _4 (.in(SP[4]));
  LED _3 (.in(SP[3]));
  LED _2 (.in(SP[2]));
  Counter #(.max('h7fff), .width(15)) counter_6 (
    .load(1'b0), .count(or_12_out), .Q(SP), .up(SP_INC), .clk(CLK), .clr(RESET));  // open: D, carry
  LED C_2 (.in(C));
  LED u_Z (.in(Z));
  LED u_O (.in(O));
  Register #(.width(1)) register_19 (.D(multiplexer_1_out[0]), .en(not_10_out), .Q(O), .clk(CLK), .clr(RESET));
  and and_17 (and_17_out, ~and_16_out, W_BUS[0]);  // AND_Gate
  _7_Segment_Display u_7_segment_display_4 (
    .g(undriven_2[7]), .f(undriven_2[6]), .a(undriven_2[5]), .b(undriven_2[4]), .e(undriven[3]),
    .d(undriven[2]), .c(undriven[1]), .dp(undriven[0]));
  LED _1 (.in(SP[1]));
  LED _0 (.in(SP[0]));
  LED u_N (.in(N));
  Register #(.width(1)) register_20 (.D(multiplexer_1_out[3]), .en(nand_1_out), .Q(N), .clk(CLK), .clr(RESET));
  and and_18 (and_18_out, ALU_SUB, ALU_ADD);
  xnor xnor_1 (xnor_1_out, W_BUS[7], xor_6_out[7]);
  xor xor_9 (xor_9_out, xor_6_out[7], controlled_buffer_25_out[7]);
  and and_19 (and_19_out, ~and_18_out, xor_8_out);  // AND_Gate
  and and_20 (and_20_out[0], xnor_1_out, xor_9_out);
  or or_13 (and_20_out[2], and_19_out, and_17_out);
  nor nor_1 (and_20_out[1], controlled_buffer_25_out[7], controlled_buffer_25_out[6], controlled_buffer_25_out[5], controlled_buffer_25_out[4], controlled_buffer_25_out[3], controlled_buffer_25_out[2], controlled_buffer_25_out[1], controlled_buffer_25_out[0]);
  ROM #(.addrWidth(11), .dataWidth(32)) _4x28C16 (
    .addr({IR_REG, T_STATE}),
    .data({T_RESET_PF, T_RESET, PC_IN, _4x28C16_data_4[0], IR_IN, MISC_SEL2, MISC_SEL1, MISC_SEL0, INSB_HO, INSB_HI, INSB_O, _4x28C16_data_3[0], O_JMP, N_JMP, Z_JMP, C_JMP, ALU_SEL2, ALU_SEL1, ALU_SEL0, _4x28C16_data_2[0], AB_SEL2, AB_SEL1, AB_SEL0, DB_TAR_SEL4, _4x28C16_data}));
  Decoder #(.enable("false"), .select(3)) decoder_4 (
    .out1(CIE), .out2(SIE), .out3(FLAG_INV), .out4(HALT), .out5(SP_INC), .out6(SP_DEC), .out7(ALU_C),
    .sel({MISC_SEL2, MISC_SEL1, MISC_SEL0}));  // open: out0
  Decoder #(.enable("false"), .select(3)) decoder_5 (
    .out0(ADDR_ABUS_OUT), .out1(SP_ABUS_OUT), .out2(PC_ABUS_OUT), .out3(IRQ_ABUS_OUT), .out4(IRQ_ABUS_OUT2),
    .out5(decoder_5_out5), .out6(decoder_5_out6), .out7(SPO_ABUS_OUT), .sel({AB_SEL2, AB_SEL1, AB_SEL0}));
  Multiplexer #(.enable("false"), .width(4)) multiplexer_1 (
    .in0({controlled_buffer_25_out[7], and_20_out}), .in1(W_BUS[3:0]), .out(multiplexer_1_out), .sel(FLAGS_IN));
  // RGB_Video #(.cursor("No Cursor"), .height(64), .scale(4)) rgb_video_1: pin names not known; wires that end beside it: RESET, CLK, rgb_video_1_p3, rgb_video_1_p4, rgb_video_1_p5, rgb_video_1_p6
  Multiplexer #(.enable("false"), .width(4)) multiplexer_2 (
    .in0(_4x28C16_data[3:0]), .in1(IR_REG2[7:4]), .out({DB_TAR_SEL3, DB_TAR_SEL2, DB_TAR_SEL1, DB_TAR_SEL0}),
    .sel(INSB_HI));
  Multiplexer #(.enable("false"), .width(4)) multiplexer_3 (
    .in0(IR_REG2[3:0]), .in1(IR_REG2[7:4]), .out(multiplexer_3_out), .sel(INSB_HO));
  Multiplexer #(.enable("false"), .width(4)) multiplexer_4 (
    .in0(_4x28C16_data[7:4]), .in1(multiplexer_3_out), .out({DB_SEL3, DB_SEL2, DB_SEL1, DB_SEL0}),
    .sel(INSB_O));
  Decoder #(.enable("false"), .select(5)) decoder_6 (
    .out1(A_IN), .out2(B_IN), .out3(C_IN), .out4(D_IN), .out5(E_IN), .out6(F_IN), .out7(G_IN), .out8(H_IN),
    .out9(FLAGS_IN), .out10(DD_IN), .out11(decoder_6_out11), .out12(decoder_6_out12), .out13(DISP_IN),
    .out14(DS_IN), .out15(IR2_IN), .out16(decoder_6_out16), .out17(OP_IN), .out18(decoder_6_out18),
    .out19(decoder_6_out19), .out20(RAM_IN), .out21(decoder_6_out21), .out22(ADDR_INH), .out23(ADDR_INL),
    .sel({DB_TAR_SEL4, DB_TAR_SEL3, DB_TAR_SEL2, DB_TAR_SEL1, DB_TAR_SEL0}));  // open: out0, out24, out25, out26, out27, out28, out29, out30, out31
  disp_ctrl disp_ctrl_1 (
    .out_5(rgb_video_1_p3), .out_6(rgb_video_1_p4), .out_7(rgb_video_1_p5), .out_8(rgb_video_1_p6),
    .in_2(DS_IN), .in_3(DD_IN), .in_4(W_BUS), .in_1(CLK));
  Decoder #(.enable("false"), .select(4)) decoder_7 (
    .out0(MEM_OUT), .out1(A_OUT), .out2(B_OUT), .out3(C_OUT), .out4(D_OUT), .out5(E_OUT), .out6(F_OUT),
    .out7(G_OUT), .out8(H_OUT), .out9(FLAGS_OUT), .out10(DUMMY_DD_OUT), .out11(ALU_OUT), .out12(PC_OUTL),
    .out13(PC_OUTH), .out14(IO_OUT), .out15(decoder_7_out15), .sel({DB_SEL3, DB_SEL2, DB_SEL1, DB_SEL0}));

  // Notes on the sheet:
  //   ADDRESS REGISTER
  //   ADDRESS BUS
  //   DATA BUS
  //   contents of rom_1 (hex, n*v repeats v):
  //   compressed eJy9l0l23DoMRedvFRjXSGzULcemzf0v4aMhJTYqx8ngH1dSEgRS5MUjgPILfS+0kF/oY6GQ7QJJ
  //   LfzEt0/AF/Lk4AHf5OwKeuUCHQvtC8WDHDnknb8OUqv7MMd4si2KhW91kniiWnK18GC1hO22UIRY
  //   vloL+yDGwULxE4Nl5S0c6CynrSeoRbw98Xp5oQfqgp2Tj9c7L1N+Hjw378dXYA4frsCJDa0ns7MV
  //   KCh+UST5dzi4zW43vWVr3nnvq60yH/YwGo7v026D7fwr2a0355RtbNlh8iVIsCAdXhYfS9DA7/Lq
  //   Ee84Hh6NC1UX4X67lFnQuYgkxAXTi2SP3vd6EQ+N+vgyjOspWvjFojSOn5j8eGWY/ZioGVcJEov2
  //   5ewai+nB2Zc3GesJCGVOlQWcK4EN997QBJa+nEYHJbDJW7BW0bGjz1Aia08/Iu7IOjp3G+vt9vgw
  //   Z2djdz0D/qe4fYkLtp/ipi6y+/dxM5fvYRZML5K0ML5IAzf6bbMcNSB/WFWNWTHefvfS0M9nsUUf
  //   W7LY4o4tldgilDntyPPnk7bztWB75UTnKy+kV3zgJEPIJV94zx5ufeVM8cXJMeuHHZyY+C8gBzmW
  //   QRz0ER+TLB/wJOyoY9mQgrjrpEEUuIidR7F7tOn5oV6xmt0uQ3cdqkPkJYHKMB6e61L4QSi3CHor
  //   0wYdow4yFe8xyBZp5e+sD4MuB1nWnuQBf5HYUkYSCvpnH/bjE+BechAW2+EieZUxMR56CxAFoIw1
  //   ar5SE3BGLd9QZWYoOzIAa+NOur9wwx/YobAjt730v8JOx8qm7pEdPlR81ONDwbfpDg2ffGswoMsq
  //   7DZjV1h27MALYGi6G/46heEqpE5Z8S5XQXkKLyu6DS8Yr1BfdGtMcliygfvEty69BZBtS+neeUeY
  //   +ZhTUDm1oMpksoJwj05qb40KSmR0vgxPfMnmtWaxaiV2Cao6C2NQDer7UC80BAwqyMnhyKgmhJzg
  //   Hy0uiC3B1GiyTGR8IXzpia+FgsUyUmsoo1KmmTIuytRTRqVMI+WSP+wFhXGSDz8Z9ViJ3tR7zGgx
  //   k51ZlrcCTx1rVTEm1naBhrVpM6imGtadxQVRbuIXC3F+xXTqgyq+YsZhgg8t5uvU5nL014o51Rgx
  //   kWiKDFW2SdOrcp8OrybM0Mu6SbpNWGSWVPPn3+l6vxMAC8OmCprlJQYFNR5krZw7WW8GFoOsO4sL
  //   i6J2D7Wph2zFqcebr4TX6LhWpA5O1StdWbVUJDxVpJIuSlbF9ZKUn6A2RcmyKh6K0gg1F6iNgK88
  //   UrJqlhRw6bUiwzlZnFelyjuTpdQr62pWwDJVeeqqPP6JqdTEq8j/EulekQ5FvgodTzy12o88a1bg
  //   IKEt8rVQoS3yBSmaIi/i0yKv1YU0da52kKUmWKIVNXPvqnT1fMmX3yfCVFughvDcBtzNU9sG4IY7
  //   tQFoBDu0Aejpzm0ALsEOmQRPgFV/F+A27fL+tJp2dK0NQEeXrAeodEtF4Z59aKVEw1tBuliiktiE
  //   9V2etQaTF+DWh77hqmiY+gbrsd70DY3gur7BKhoaqd19QyE79w1lsim/lizb9w21weLfRq9Fq/xY
  //   yWQ3T5VM24e2azCwGCqZpli1FM5L00VRjB1o2258k3H/7+4s1Pbs7hv+tT2rGfeCQsG6Boysr1KG
  //   nnUpZU9ZOBaLTEJjVTuO2j9wwlhDTReyZd31dmXmH/ph2zZa4k0LgVST8dxCiAyfD761EPTcQqCN
  //   kDUiDz/B2vbsqWezJrAmD03CuWsh8MC9NmljZ7zp+TDA8i8HMsPWBkQth0l9u2iffwG5K3r3T1vM
  //   RW/+efb00xaPjcT482zpw/OLn2dt4VNGGU2r3TUUKOWwbSgElLtKHJUSh07ZkkV6C/4DtSKkoA==
  //   JUMP LOGIC
  //   32K ROM
  //   PROGRAM COUNTER
  //   32K RAM
  //   INSTRUCTION REGISTER
  //   INSTRUCTION REGISTER 2
  //   OP REG
  //   A REG
  //   B REG
  //   C REG
  //   D REG
  //   E REG
  //   F REG
  //   G REG
  //   H REG
  //   T STATE
  //   contents of rom_2 (hex, n*v repeats v):
  //   compressed eJztmE1u7LoOhOdehZdw3AQYezndUnH/S3giP/EAmQQBzuQN7qT1Y5HFKtJ0oi+d1+v8jPPj53yd
  //   8lM67XWEznitR1/5/MrZOrN+fP3MXMqP9ZNPLZeRs0hPy+Izymd6HR8/PmPmcvleP/nUchk5SwtP
  //   C79ex8crjoXx8bTwtPC08LTwtPB4HTOjmhnVzKjmq2KfuVTOlE8tz0XOImktCy2M9bMslBjy4rt4
  //   KDGUGEqM9bNmSgulhdJCi4eUFiqN0kJpobTQsrCMylZUh2VUllFZRmUZlb1KV8tl5CxS42URiRGJ
  //   sX58/cxcKmfKp5WLzEZiRGJEMo/EiMSIxIjMRyRGJEa8Kn87g5XDL12sKo9fySeHyaacgZPGZrAq
  //   L38rYfHLn/Ky62FXRNYEAyeNzWAVaVfVkcOuKGpqlJeqkhzESpw07IJVxVIVkwNefFcmXhwvXvVZ
  //   1ZODsYkXLy8TRpPqnjDKWjpymGyKehcnjc1gFbwG5SVrK98HYhGxyPebIlbipLEZrEoXkSORI5Gj
  //   rLka8EKORI6y9soOL+TIYGQwMhgZOTIYGe+t9ZtrbAar4E0uL0EsQSxBvQSxBLEEsYR2B6AHEEsQ
  //   S1AvQSxBLEEsgbpBLLH7SHeSpUtWS3WTqt0cqqNk7dYw2RQrcdKwC1bVkap2c7hYlZeq3Rwmm8o+
  //   VbWbg7EZrIJuVl7+9ja6G/1td7jd43aX231udzp63aDbDfrdoOMNet6g6w363qDzDXrfoPuN6n+J
  //   Vl4mjCaMJowmjKp2a+CkYResgoZcXqov5lBeRCzy3bOXLl//fSP++0b8n38j7j/7K8Fk+WWi3lkW
  //   TGY/+vTOQmBytZ8vrKpa96R3rHfUO9tzMWSydNuTsXeufrQ9l2J70jvWO+od4acywGTHXBlicvWj
  //   8vznTxBzTXqn9MmJeqdizsnsw5/eKc85ufpRe14xH3vSO7bPqD2rPas9qz2rPetqP9uzdczWMdvL
  //   eke9sz1bx2zoXJOxd65+tD1L27M6ZnXM6piFzjmZ/WjHrI5ZuvpRe/b27O3Zt87VK/Zk+/H27O3Z
  //   27O3Z9+esxsde9I7O+bZasxWY7YaszM4W43sftvP9vzpmD8dc3VNJuqd7fnTMWe3PfZk7J2rH7Xn
  //   0Z5Hex7tebTnsXXe72BOdsz7HcxJex7b89W1cbUaV9fz1WpcrcbValytxtVqXF0bV6uRpX3sSe/s
  //   mDPPPfE9mf3o0zvbc7o88v378+fM97GGz2DwGiabYiVO2to88v2vVXAk3jUMNh0vDyux0gKtvrxW
  //   yaqGwkvWNUw2xUqcLLxUsVbBkcK7XoNNx8vDSqwKL/OxVpmfGgov81fDZFOsxMnCy3qoVXCk8D5j
  //   sOl4eViJFXgOnoPn4Dl4Dp6D5+A5eA6eg+fgOXgOnoPn4HnhTfSc6DnRc6LnRM+JnhM9J3pO9Jzo
  //   OdFzoudEz4meEz0negp+gp/gJ/gJfoKf4Cf4CX6Cn+An+Al+gp/gJ/iJ+hT1KepT1KeoT1Gfoj5F
  //   fYr6FPUp6lPUp6hPUZ+iPkV9Gnoaehp6Gnoaehp6Gnoaehp6Gnoaehp6Gnoaehp6GnoG/AJ+Ab+A
  //   X8Av4BfwC/gF/AJ+Ab+AX8Av4BfwC/gF/AJ+Ab+AX8Av4BfwC/gF/AJ+Ab+AX8Av4Bfwi83vDd4b
  //   vDd4b/De4L3Be4P3Bu8N3hu8N3hv8N7gvcF7g/cuvIGeAz0Heg70HOg50HOg50DPgZ4DPQd6DvQc
  //   6DnQc6DnQE+nvzj9xekvTn9x+ovTX5z+4vQXp784/cXpL05/cfqL01+c/uL0lwd+D/we+D3we+D3
  //   wO+B3wO/B34P/B74PfB74PfA74HfAz/BT/AT/AQ/wU/wE/wEP8FP8BP8BD/BT/AT/AQ/3eDd4N3g
  //   3eDd4N3g3eDd4N3g3eDd4N3g3eDd4N3g3YWX37/1Xc2f9Z3NYX0da/AaJptiJU5afjfre5xD2dX3
  //   ugavYbIpVuJk2dVfCDmUXf0FUYPXMNkUK3ESO8fOsXPsHDvHzrFz7LzsJnFO4pzEOYlzEuckzkmc
  //   kzgFnsATeAJP4Ak8gSfwhJ5CT6Gn0FPoKfQUego9jTiNOI04jTiNOI04jTiz8x4//A94/vA/4PHt
  //   v77z1//1/ctd4O9u/85vt3/HD/d95w/3fce3G77z1zd8/3Cn98tbvPPbLd4/3JX98nbs/HY7dvxw
  //   H3b+cB92fLsBO399A/YPd16/vOVi4CR26Cn0FHoKPYWe0r6vwg49jTiNOI04jTiNOI047bVvutLO
  //   yZ+TPyd/Tv6c/Dn5c/Ln5M/Jn5M/J39O/pz8Oflz8ufkz8mfkz8nf07+nPw5+XPy5+TP910c+fO/
  //   93HYcSe3b+X2vRz5c/Ln5M/Jn5M/J39O/pz8Oflz8ufkz8mfkz9X3wFyCwge+XPy5+TPyZ+TPyd/
  //   Tv6c/Dn5c/Ln5M/Jn5M/J39O/pz8eeXvfzQ8BsM=
  //   STACK POINTER
  //   ALU REG
  //   DISPLAY DECODER ROM (4x1Kx8)
  //   FLAGS
  //   contents of _4x28C16 (hex, n*v repeats v):
  //   compressed eJztWduSgyAMfecreN4nsKnYz2ld/P9PWK4alCBqZ1a3uzNdcUgCyUmOXDohNAjBzU8L82y/TMs3
  //   u9DVx0amT99Fy8w/xdvYBXkp7qTMm5xJsYzUbSG1tMXMW1Mx4o2UYsm8uipbToqt+QglWyzaIqXu
  //   5nkz5vwzG9sxav2DRqd/0n2tew4mik87CPD7UmZKiiH8TY4YXQ53ELoxk8no9t/02GAda4TM9HlM
  //   7ORCUunbN3B96wFFYdGIymo9cBXOsYLfm7rYLq15Fzs6jYN+eagFeBsZqJ1A37UheQkBlPrWVh5I
  //   UtWWu9HSRFlZqUZoabB/2odCsxbe87UBuB5iBZtWGC+vMpa6H8m9+lqiVMqRtw1cDDhvRAPiQVHv
  //   SDi2SxKkGgS0EaCwSULHJnsV+CSx8NVb0D+WpGMeRbfchGE0XwWz0xqs1pJ8zl/4M9SlzPkxfh+N
  //   o3Irs5+Exqa8lCYvG2ug7ywHvTbxxiHlsNBAc+BLM1kikYyU31ILqLqsK82oL19AWyyWUJygbzU6
  //   6g8vKJXPNAesUVV5fuYyLiRfsrwUc9GeyZOeTu6safxqreNkVrPMyISukM17tN9em/vY+/yc83a/
  //   EO6GEGCFEGjYjyiHRVcgMcLMwfROaQpGQijSFJ/VPF4gYp4jqMvuntiCiErUBStkl6cuIKgrs291
  //   bkCZiM6W2DNq2ppmLKGm3do4gLSdf5L5bb/wsqorg83msP3ZoFzaL7dxDYg+t35j/mpQLu0XrtEe
  //   I/q/VjyzXw42W4HJZnXboaz7hibLoitu/S+dMg5G5XHkFTh+UmzO71cowtyJT+WGIT3FqN4IxVOM
  //   zVsUKenTlU9G8u1+4dRQew4Vk9ywV1WVx3koPZS/8ixte/MZ4kZDSZK7wfxATN/ul0YHPn1nNrJO
  //   nr4Rk7wgld0dT/IU4vNTY9sP+RwpqcYjmem2ASiV5FhG+OvvmtFKgUynr4kA+QgaAZD5m8d58Lzo
  //   hVbCKnYJdBWulXXrIRRbXIqzH6LYFaY=
  //   MICROCODE
  //   INSTRUCTION DECODER ROM (4x2Kx8)
endmodule

module disp_ctrl (
  input  in_1,
  input  in_2,
  input  in_3,
  input  [7:0] in_4,
  output out_5,
  output [6:0] out_6,
  output [5:0] out_7,
  output [2:0] out_8
);

  wire and_1_out, and_2_out, and_3_out, decoder_1_out7, decoder_1_out8, multiplexer_1_out, register_3_q;
  wire [3:3] counter_2_q;
  wire [7:0] register_2_q;

  and and_1 (and_1_out, ~in_4[7], in_4[6], ~register_3_q);  // AND_Gate
  and and_2 (and_2_out, in_4[7], ~in_4[6], in_4[5], in_4[4], in_4[3], ~register_3_q);  // AND_Gate
  and and_3 (and_3_out, in_3, register_3_q);
  Counter #(.max('h3f), .width(6)) counter_1 (
    .load(and_1_out), .D(in_4[5:0]), .count(decoder_1_out7), .Q(out_6[5:0]), .clk(in_1));  // open: carry, clr
  Register #(.width(3)) register_1 (.D(in_4[2:0]), .en(and_2_out), .Q(out_7[5:3]), .clk(in_1));  // open: clr
  Register register_2 (.D(in_4), .en(and_3_out), .Q(register_2_q), .clk(in_1));  // open: clr
  Register #(.width(1)) register_3 (.D(in_4[0]), .en(in_2), .Q(register_3_q), .clk(in_1));  // open: clr
  Counter #(.max('hf), .width(4)) counter_2 (
    .count(out_5), .Q({counter_2_q[3], out_7[2:0]}), .clk(in_1), .clr(and_3_out));  // open: load, D, carry
  Register #(.width(1)) register_4 (.D(in_4[1]), .en(in_2), .Q(out_6[6]), .clk(in_1));  // open: clr
  Multiplexer #(.enable("false"), .select(3)) multiplexer_1 (
    .in0(register_2_q[0]), .in1(register_2_q[1]), .in2(register_2_q[2]), .in3(register_2_q[3]),
    .in4(register_2_q[4]), .in5(register_2_q[5]), .in6(register_2_q[6]), .in7(register_2_q[7]),
    .out(multiplexer_1_out), .sel(out_7[2:0]));
  not not_1 (out_8[1], multiplexer_1_out);
  Decoder #(.enable("false"), .select(4)) decoder_1 (
    .out7(decoder_1_out7), .out8(decoder_1_out8), .sel({counter_2_q[3], out_7[2:0]}));  // open: out0, out1, out2, out3, out4, out5, out6, out9, out10, out11, out12, out13, out14, out15
  not not_2 (out_5, decoder_1_out8);

  assign {out_8[2], out_8[0]} = 2'b00;
endmodule
